// Logisim project s-mips.circ as structural Verilog
module S_MIPS_Board (
  input  DESHABILITAR_DISPATCHER,
  output halt
);

  wire button_1_out, CLK, CS, d_ff_1_q, LCLR, LoadRAM, LoadRAMOn, LW, R_R_W, R_W, ram_dispatcher_1_finished,
       RCS, Reset_out, RST, TTY_EN;
  wire [2:0] KDB;
  wire [3:0] LMask, Mask, ram_1_read_time, ram_1_write_time, RMask;
  wire [6:0] KDB_DATA, TTY_DATA;
  wire [15:0] Addr, LAddr, RAddr;
  wire [31:0] I0, I1, I2, I3, LData, ram_1_data_out_0, ram_1_data_out_1, ram_1_data_out_2, ram_1_data_out_3,
       RI0, RI1, RI2, RI3;

  TTY #(.rows(25), .cols(80)) tty_1 (.data(TTY_DATA), .clk(CLK), .we(TTY_EN), .clr(RST));
  not not_1 (LoadRAMOn, ram_dispatcher_1_finished);
  RAM_Dispatcher ram_dispatcher_1 (
    .WriteTime(ram_1_write_time), .Clock(CLK), .Data(LData), .Address(LAddr), .Mask(LMask),
    .Finished(ram_dispatcher_1_finished), .Write(LW), .CLR(LCLR));
  Keyboard #(.buflen(64)) keyboard_1 (.clk(CLK), .re(KDB[0]), .avail(KDB[2]), .data(KDB_DATA));  // open: clr
  RAM ram_1 (
    .Address(RAddr), .Data_Out_0(ram_1_data_out_0), .Data_Out_1(ram_1_data_out_1),
    .Data_Out_2(ram_1_data_out_2), .Data_Out_3(ram_1_data_out_3), .Data_In_0(RI0), .Data_In_1(RI1),
    .Data_In_2(RI2), .Data_In_3(RI3), .Mask(RMask), .nRead_Write(R_R_W), .Chip_Select(RCS),
    .Read_Time(ram_1_read_time), .Reset(button_1_out), .Write_Time(ram_1_write_time));
  Button button_1 (.out(button_1_out));
  D_Flip_Flop d_ff_1 (.clk(CLK), .D(1'b1), .Q(d_ff_1_q), .reset(Reset_out));  // open: Qn, preset, en
  Button Reset (.out(Reset_out));
  S_MIPS s_mips_1 (
    .Kbd_Enable(KDB[0]), .Address(Addr), .Kbd_Clear(KDB[1]), .Kbd_Available(KDB[2]), .RAM_In_0(I0),
    .Kbd_ASCII_Data(KDB_DATA), .RAM_In_1(I1), .TTY_Enable(TTY_EN), .RAM_In_2(I2), .RAM_In_3(I3),
    .TTY_ASCII_Data(TTY_DATA), .Reset(RST), .RAM_Out_0(ram_1_data_out_0), .Clock(CLK),
    .RAM_Out_1(ram_1_data_out_1), .Stop(halt), .RAM_Out_2(ram_1_data_out_2), .RAM_Out_3(ram_1_data_out_3),
    .Mask(Mask), .Read_Time(ram_1_read_time), .Write_Time(ram_1_write_time), .nRead_Write(R_W),
    .Chip_Select(CS));
  D_Flip_Flop d_ff_2 (.clk(CLK), .D(d_ff_1_q), .Qn(LCLR), .reset(Reset_out));  // open: Q, preset, en
  or or_1 (RST, LCLR, LoadRAM);
  Clock clock_1 (.out(CLK));
  Multiplexer #(.width(32), .enable("false")) multiplexer_1 (.in0(I0), .in1(LData), .out(RI0), .sel(LoadRAM));
  Multiplexer #(.width(32), .enable("false")) multiplexer_2 (.in0(I1), .in1(LData), .out(RI1), .sel(LoadRAM));
  Multiplexer #(.width(32), .enable("false")) multiplexer_3 (.in0(I2), .in1(LData), .out(RI2), .sel(LoadRAM));
  Multiplexer #(.width(32), .enable("false")) multiplexer_4 (.in0(I3), .in1(LData), .out(RI3), .sel(LoadRAM));
  and and_1 (LoadRAM, ~DESHABILITAR_DISPATCHER, LoadRAMOn);  // AND_Gate
  Multiplexer #(.width(16), .enable("false")) multiplexer_5 (.in0(Addr), .in1(LAddr), .out(RAddr), .sel(LoadRAM));
  Multiplexer #(.width(4), .enable("false")) multiplexer_6 (.in0(Mask), .in1(LMask), .out(RMask), .sel(LoadRAM));
  Multiplexer #(.enable("false")) multiplexer_7 (.in0(CS), .in1(LW), .out(RCS), .sel(LoadRAM));
  Multiplexer #(.enable("false")) multiplexer_8 (.in0(R_W), .in1(LW), .out(R_R_W), .sel(LoadRAM));

  // Notes on the sheet:
  //   NO MODIFICAR
  //   Keyboard
endmodule

module RAM (
  input  [15:0] Address,
  input  [31:0] Data_In_0,
  input  [31:0] Data_In_1,
  input  [31:0] Data_In_2,
  input  [31:0] Data_In_3,
  input  [3:0] Mask,
  input  nRead_Write,
  input  Chip_Select,
  input  Reset,
  output [31:0] Data_Out_0,
  output [31:0] Data_Out_1,
  output [31:0] Data_Out_2,
  output [31:0] Data_Out_3,
  output [3:0] Read_Time,
  output [3:0] Write_Time
);

  wire and_2_out, and_3_out, and_4_out, and_5_out, and_6_out, and_7_out, and_8_out, and_9_out, Changed, CLK,
       comparator_2_eq, comparator_3_eq, comparator_4_eq, comparator_5_eq, comparator_6_eq, Count,
       demultiplexer_3_out0, Idle, Idle_q, Load, Load0, Load1, nand_1_out, or_1_out, or_2_out, or_3_out,
       or_4_out, or_5_out, or_6_out, or_7_out, or_8_out, or_9_out, or_10_out, Proc_q, Update_Mem, Zero_Time;
  wire [3:0] counter_1_q, multiplexer_1_out, subtractor_1_out;
  wire [31:0] register_1_q, register_2_q, register_3_q, register_4_q, register_5_q;

  // Probe on 4'b0011
  // Probe on 4'b0010
  Multiplexer #(.width(4), .enable("false")) multiplexer_1 (
    .in0(4'b0011), .in1(4'b0010), .out(multiplexer_1_out), .sel(nRead_Write));
  or or_1 (or_1_out, Idle, Update_Mem);
  or or_2 (or_2_out, ~Chip_Select, Reset);  // OR_Gate
  Subtractor #(.width(4)) subtractor_1 (.a(multiplexer_1_out), .b(4'b0010), .out(subtractor_1_out));  // open: bin, bout
  Demultiplexer #(.enable("false")) demultiplexer_1 (.out0(Idle), .out1(Load0), .in(Idle_q), .sel(Changed));
  D_Flip_Flop u_Idle (.clk(CLK), .D(or_1_out), .Q(Idle_q), .preset(or_2_out));  // open: Qn, en, reset
  // Probe on counter_1_q
  Counter #(.width(4), .max('hf)) counter_1 (
    .load(Load), .D(subtractor_1_out), .count(Count), .Q(counter_1_q), .clk(CLK), .clr(or_3_out));  // open: carry
  or or_3 (or_3_out, ~Chip_Select, Reset);  // OR_Gate
  Comparator #(.width(4), .mode("unsigned")) comparator_1 (
    .a(4'b0000), .b(counter_1_q), .eq(Zero_Time));  // open: gt, lt
  or or_4 (or_4_out, Count, Load0, Load1);
  Register #(.width(32)) register_1 (.D(Data_In_0), .en(Chip_Select), .Q(register_1_q), .clk(CLK), .clr(or_5_out));
  or or_5 (or_5_out, ~Chip_Select, Reset);  // OR_Gate
  Register #(.width(32)) register_2 (.D(Data_In_1), .en(Chip_Select), .Q(register_2_q), .clk(CLK), .clr(or_6_out));
  or or_6 (or_6_out, ~Chip_Select, Reset);  // OR_Gate
  Register #(.width(32)) register_3 (.D(Data_In_2), .en(Chip_Select), .Q(register_3_q), .clk(CLK), .clr(or_7_out));
  or or_7 (or_7_out, ~Chip_Select, Reset);  // OR_Gate
  Register #(.width(32)) register_4 (.D(Data_In_3), .en(Chip_Select), .Q(register_4_q), .clk(CLK), .clr(or_8_out));
  or or_8 (or_8_out, ~Chip_Select, Reset);  // OR_Gate
  Register #(.width(32)) register_5 (
    .D({{11{1'b1}}, nRead_Write, Mask, Address}), .en(Chip_Select), .Q(register_5_q), .clk(CLK),
    .clr(or_9_out));
  or or_9 (or_9_out, ~Chip_Select, Reset);  // OR_Gate
  D_Flip_Flop Proc (.clk(CLK), .D(or_4_out), .Q(Proc_q), .reset(or_10_out));  // open: Qn, preset, en
  or or_10 (or_10_out, ~Chip_Select, Reset);  // OR_Gate
  Demultiplexer #(.enable("false")) demultiplexer_2 (
    .out0(Count), .out1(Update_Mem), .in(demultiplexer_3_out0), .sel(Zero_Time));
  Demultiplexer #(.enable("false")) demultiplexer_3 (
    .out0(demultiplexer_3_out0), .out1(Load1), .in(Proc_q), .sel(Changed));
  Clock clock_1 (.out(CLK));
  Comparator #(.width(32)) comparator_2 (.a(register_1_q), .b(Data_In_0), .eq(comparator_2_eq));  // open: gt, lt
  Comparator #(.width(32)) comparator_3 (.a(register_2_q), .b(Data_In_1), .eq(comparator_3_eq));  // open: gt, lt
  Comparator #(.width(32)) comparator_4 (.a(register_3_q), .b(Data_In_2), .eq(comparator_4_eq));  // open: gt, lt
  Comparator #(.width(32)) comparator_5 (.a(register_4_q), .b(Data_In_3), .eq(comparator_5_eq));  // open: gt, lt
  Comparator #(.width(32)) comparator_6 (
    .a(register_5_q), .b({{11{1'b1}}, nRead_Write, Mask, Address}), .eq(comparator_6_eq));  // open: gt, lt
  nand nand_1 (nand_1_out, comparator_6_eq, comparator_2_eq, comparator_3_eq, comparator_4_eq, comparator_5_eq);
  and and_1 (Changed, nand_1_out, Chip_Select);
  or or_11 (Load, Count, Load1, Load0);
  and and_2 (and_2_out, Mask[0], Update_Mem, nRead_Write);
  and and_3 (and_3_out, Mask[1], Update_Mem, nRead_Write);
  and and_4 (and_4_out, Mask[2], Update_Mem, nRead_Write);
  and and_5 (and_5_out, Mask[3], Update_Mem, nRead_Write);
  RAM_part #(.addrWidth(16), .dataWidth(32), .bus("separate")) ram_1 (
    .addr(Address), .din(Data_In_0), .data(Data_Out_0), .str(and_2_out), .sel(Chip_Select), .clk(CLK),
    .ld(and_6_out), .clr(Reset));
  and and_6 (and_6_out, ~nRead_Write, Idle);  // AND_Gate
  RAM_part #(.addrWidth(16), .dataWidth(32), .bus("separate")) ram_2 (
    .addr(Address), .din(Data_In_1), .data(Data_Out_1), .str(and_3_out), .sel(Chip_Select), .clk(CLK),
    .ld(and_7_out), .clr(Reset));
  and and_7 (and_7_out, ~nRead_Write, Idle);  // AND_Gate
  RAM_part #(.addrWidth(16), .dataWidth(32), .bus("separate")) ram_3 (
    .addr(Address), .din(Data_In_2), .data(Data_Out_2), .str(and_4_out), .sel(Chip_Select), .clk(CLK),
    .ld(and_8_out), .clr(Reset));
  and and_8 (and_8_out, ~nRead_Write, Idle);  // AND_Gate
  RAM_part #(.addrWidth(16), .dataWidth(32), .bus("separate")) ram_4 (
    .addr(Address), .din(Data_In_3), .data(Data_Out_3), .str(and_5_out), .sel(Chip_Select), .clk(CLK),
    .ld(and_9_out), .clr(Reset));
  and and_9 (and_9_out, ~nRead_Write, Idle);  // AND_Gate

  assign Read_Time = 4'b0011;
  assign Write_Time = 4'b0010;

  // Other names for the same wires on the sheet: M0 = Mask[0]; M1 = Mask[1]; M2 = Mask[2]; M3 = Mask[3];
  //   RW = nRead_Write; CLR = Reset; CS = Chip_Select; Load2 = Count

  // Notes on the sheet:
  //   NO MODIFICAR
  //   excepto quizás los valores RT y WT
  //   BANK0
  //   BANK1
  //   BANK2
  //   BANK3
endmodule

module RAM_Dispatcher (
  input  [3:0] WriteTime,
  input  Clock,
  input  CLR,
  output [31:0] Data,
  output [15:0] Address,
  output [3:0] Mask,
  output Finished,
  output Write
);

  wire demultiplexer_2_out1, demultiplexer_3_out1, End, IDLE_q, IncAddr, Load, or_1_out, or_2_out, While_q,
       WriteEnd;
  wire [3:0] counter_1_q;
  wire [31:0] CurrentAddress_q;

  Counter #(.width(32), .max('hffffffff)) CurrentAddress (
    .count(IncAddr), .Q({CurrentAddress_q[31:18], Address, CurrentAddress_q[1:0]}), .clk(Clock), .clr(CLR));  // open: load, D, carry
  or or_1 (or_1_out, IncAddr, demultiplexer_3_out1, Finished);
  D_Flip_Flop IDLE (.clk(Clock), .D(or_1_out), .Q(IDLE_q), .preset(CLR));  // open: Qn, en, reset
  Demultiplexer #(.enable("false")) demultiplexer_1 (.out0(Load), .out1(Finished), .in(IDLE_q), .sel(End));
  D_Flip_Flop While (.clk(Clock), .D(or_2_out), .Q(While_q), .reset(CLR));  // open: Qn, preset, en
  or or_2 (or_2_out, Write, Load);
  RAM_part #(.addrWidth(18), .dataWidth(32)) ram_1 (
    .addr({Address, CurrentAddress_q[1:0]}), .data(Data), .clk(Clock));  // open: sel, ld, clr
  Demultiplexer #(.enable("false")) demultiplexer_2 (
    .out0(Write), .out1(demultiplexer_2_out1), .in(While_q), .sel(WriteEnd));
  Decoder #(.select(2)) decoder_1 (
    .out0(Mask[0]), .out1(Mask[1]), .out2(Mask[2]), .out3(Mask[3]), .sel(CurrentAddress_q[1:0]));  // open: en
  Demultiplexer #(.enable("false")) demultiplexer_3 (
    .out0(IncAddr), .out1(demultiplexer_3_out1), .in(demultiplexer_2_out1), .sel(End));
  Counter #(.width(4), .max('hf)) counter_1 (
    .load(Load), .D(WriteTime), .count(Write), .Q(counter_1_q), .clk(Clock));  // open: carry, clr
  Comparator #(.width(32)) comparator_1 (.a(Data), .b({32{1'b1}}), .eq(End));  // open: gt, lt
  Comparator #(.width(4)) comparator_2 (.a(4'b0000), .b(counter_1_q), .eq(WriteEnd));  // open: gt, lt

  // Other names for the same wires on the sheet: CLK = Clock; Count = Write; WT[3:0] = WriteTime
endmodule

module S_MIPS (
  input  Kbd_Available,
  input  [6:0] Kbd_ASCII_Data,
  input  [31:0] RAM_Out_0,
  input  [31:0] RAM_Out_1,
  input  Reset,
  input  [31:0] RAM_Out_2,
  input  Clock,
  input  [31:0] RAM_Out_3,
  input  [3:0] Read_Time,
  input  [3:0] Write_Time,
  output Kbd_Enable,
  output [15:0] Address,
  output Kbd_Clear,
  output TTY_Enable,
  output [6:0] TTY_ASCII_Data,
  output Stop,
  output [31:0] RAM_In_0,
  output [31:0] RAM_In_1,
  output [31:0] RAM_In_2,
  output [31:0] RAM_In_3,
  output [3:0] Mask,
  output nRead_Write,
  output Chip_Select
);

  wire Finish_Fetch, Finish_Mem, Ins_Cache_Enable, Is_jump, Is_Rnd, IsPop, IsPush, LoadPc, Mem_Cache_Enable,
       Mem_Write_Last_Op, MulorDiv, PutZeros, RegWrite, RW_in, Sel_Ram_Address, Sel_SP_Addr, SelReg_Address;
  wire [1:0] Sel_Hi, SelOpB, SelRegIn;
  wire [3:0] Alu_Op;
  wire [5:0] Fun_Code, Op_Code;

  CONTROL_UNIT_2 control_unit_1 (
    .CLK(Clock), .Alu_Op(Alu_Op), .Mem_Write(RW_in), .Finish_Instruction_Fetch(Finish_Fetch), .RESET(Reset),
    .Is_Jump(Is_jump), .Mul_or_Div(MulorDiv), .Finish_Mem_Section(Finish_Mem), .Sel_SP_Addr(Sel_SP_Addr),
    .Sel_Reg_Address(SelReg_Address), .Op_Code(Op_Code), .Instr_Cache_Enable(Ins_Cache_Enable),
    .SelOpB(SelOpB), .Put_Zeros(PutZeros), .Fun_Code(Fun_Code), .SelRegIn(SelRegIn), .IsPop(IsPop),
    .Mem_Cache_Enable(Mem_Cache_Enable), .Halt___Stop(Stop), .Reg_Write(RegWrite), .IsPush(IsPush),
    .Tty_Enable(TTY_Enable), .Mem_Write_LastOp(Mem_Write_Last_Op), .Load_Pc(LoadPc), .is_rnd(Is_Rnd),
    .Sel_Hi(Sel_Hi), .Sel_Ram_Address(Sel_Ram_Address), .Kbd_Enable(Kbd_Enable));
  Data_Path data_path_1 (
    .CLK(Clock), .Reset(Reset), .Ram_Out_0(RAM_Out_0), .Ram_Out_1(RAM_Out_1), .Ram_Out_2(RAM_Out_2),
    .Read_Time(Read_Time), .Write_Time(Write_Time), .Ram_Out_3(RAM_Out_3), .Read_Write_Reg(RegWrite),
    .MulorDiv(MulorDiv), .Alu_Op(Alu_Op), .Is_Push(IsPush), .Memory_RW(RW_in), .Is_Pop(IsPop),
    .Is_Jump_Instr(Is_jump), .random(Is_Rnd), .Load_New_PC(LoadPc), .Put_Zeros(PutZeros), .Sel_Op_B(SelOpB),
    .Sel_Ram_Address(Sel_Ram_Address), .Sel_SP_Addr(Sel_SP_Addr), .Sel_Hi(Sel_Hi), .Sel_Reg_Input(SelRegIn),
    .Sel_Reg_Address(SelReg_Address), .Ins_Cache_En(Ins_Cache_Enable), .Mem_Cache_En(Mem_Cache_Enable),
    .Ram_IN_0(RAM_In_0), .Ram_IN_1(RAM_In_1), .Ram_IN_2(RAM_In_2), .Ram_IN_3(RAM_In_3), .CS(Chip_Select),
    .Mask_for_RAM(Mask), .Ram__ADDRESS(Address), .RW_Out(nRead_Write),
    .Finish_Instruction_Fetch(Finish_Fetch), .Finish_Mem_Section(Finish_Mem), .kbd_available(Kbd_Available),
    .kbd_data(Kbd_ASCII_Data), .Tty(TTY_ASCII_Data), .MEM_WRITE_LAST_OP(Mem_Write_Last_Op),
    .Op_Code(Op_Code), .Fun_Code(Fun_Code));

  assign Kbd_Clear = Reset;

  // Other names for the same wires on the sheet: CLK = Clock; CS = Chip_Select; KBD_AVAIL = Kbd_Available;
  //   CLR = Reset; KBD_CLR = Reset; KBD_DATA[6:0] = Kbd_ASCII_Data; RAM_A[15:0] = Address;
  //   RAM_INPUT_0[31:0] = RAM_In_0; RAM_INPUT_1[31:0] = RAM_In_1; RAM_INPUT_2[31:0] = RAM_In_2;
  //   RAM_INPUT_3[31:0] = RAM_In_3; RAM_MASK[3:0] = Mask; RAM_OUTPUT_0[31:0] = RAM_Out_0;
  //   RAM_OUTPUT_1[31:0] = RAM_Out_1; RAM_OUTPUT_2[31:0] = RAM_Out_2; RAM_OUTPUT_3[31:0] = RAM_Out_3;
  //   RW = nRead_Write; TTY_DATA[6:0] = TTY_ASCII_Data

  // Notes on the sheet:
  //   RAM ADDRESS
  //   DATA FROM RAM
  //   DATA TO RAM
  //   DATA WRITE MASK
  //   RAM TIMING
  //   RAM CONTROL
  //   KEYBOARD
  //   TTY
  //   SEQUENCING
endmodule

module Instruction_Decoder (
  input  [5:0] Op_Code,
  input  [5:0] Fun_Code,
  output [3:0] Alu_Op,
  output [1:0] SelOpB,
  output jmp,
  output [1:0] SelRegIn,
  output [1:0] Sel_Hi,
  output [2:0] Path,
  output Is_Sw,
  output Logical_Inmediate,
  output Is_Push,
  output [1:0] Especial,
  output Is_Pop
);

  wire Add, add___sub___slt___stlu___and___or___nor___xor, Add_or_Sub, addi, And, and_7_out, and___andi,
       andi, beq, bgtz, blez, blez___bgtz___bltz, bltz, bne, cmp_set_1, cmp_set_2, comparator_2_eq,
       comparator_3_eq, comparator_4_eq, comparator_5_eq, comparator_6_eq, comparator_8_eq, comparator_11_eq,
       comparator_12_eq, comparator_13_eq, comparator_15_eq, comparator_16_eq, comparator_17_eq, Div, Divu,
       halt, Inmediate, Is_Mul_Or_Div, j, jr, kbd, lw, lw_or_sw, mfhi, mflo, mul___div, Mult, Mulu,
       mulu___divu, Nor, Op_code_is_0, Or, or_1_out, or___ori, ori, rnd, slt, slti, sltiu, sltu,
       sltu___sltiu___slt___slti, sltu_or_sltiu, Special, Sub, tty, Xor, xor___xori, xori;

  or or_1 (or_1_out, Div, Divu);
  Comparator #(.width(6), .mode("unsigned")) comparator_1 (
    .a(Op_Code), .b({6{1'b0}}), .eq(Op_code_is_0));  // open: gt, lt
  or or_2 (SelOpB[0], lw_or_sw, Inmediate);
  or or_3 (SelRegIn[0], lw, Is_Pop, mflo);
  or or_4 (Alu_Op[0], Sub, beq, bne, or_1_out, Is_Push, or___ori, xor___xori, sltu_or_sltiu);
  or or_5 (Alu_Op[2], mulu___divu, and___andi, or___ori, blez___bgtz___bltz);
  or or_6 (SelRegIn[1], mfhi, mflo);
  or or_7 (Alu_Op[1], mul___div, and___andi, or___ori, sltu___sltiu___slt___slti);
  or or_8 (Alu_Op[3], Nor, xor___xori, sltu___sltiu___slt___slti, blez___bgtz___bltz);
  // Probe on Alu_Op
  or or_9 (jmp, bltz, beq, bne, blez, bgtz, j, jr);
  or or_10 (Especial[0], tty, kbd);
  or or_11 (Especial[1], rnd, kbd);
  or or_12 (Path[0], lw_or_sw, Is_Mul_Or_Div, SelOpB[1], Special);
  or or_13 (Path[1], add___sub___slt___stlu___and___or___nor___xor, Is_Mul_Or_Div, SelRegIn[1], Special);
  or or_14 (Path[2], Inmediate, SelOpB[1], SelRegIn[1], Special);
  // Probe on Alu_Op
  or or_15 (Sel_Hi[0], Mulu, Divu);
  or or_16 (Sel_Hi[1], Divu, Div);
  or or_17 (Logical_Inmediate, andi, ori, xori);
  Comparator #(.width(6), .mode("unsigned")) comparator_2 (
    .a(Fun_Code), .b({6{1'b1}}), .eq(comparator_2_eq));  // open: gt, lt
  Comparator #(.width(4), .mode("unsigned")) comparator_3 (
    .a(Fun_Code[5:2]), .b(4'b0110), .eq(comparator_3_eq));  // open: gt, lt
  Comparator #(.width(4), .mode("unsigned")) comparator_4 (
    .a(Fun_Code[5:2]), .b(4'b1000), .eq(comparator_4_eq));  // open: gt, lt
  Comparator #(.width(4), .mode("unsigned")) comparator_5 (
    .a(Fun_Code[5:2]), .b(4'b1001), .eq(comparator_5_eq));  // open: gt, lt
  Comparator #(.width(3), .mode("unsigned")) comparator_6 (
    .a(Op_Code[5:3]), .b(3'b000), .eq(comparator_6_eq));  // open: gt, lt
  and and_1 (halt, Special, comparator_2_eq);
  and and_2 (Is_Mul_Or_Div, Op_code_is_0, comparator_3_eq);
  // Probe on 4'b0110
  and and_3 (Add_or_Sub, Op_code_is_0, comparator_4_eq);
  and and_4 (cmp_set_1, Op_code_is_0, comparator_5_eq);
  Demultiplexer #(.select(3), .enable("false")) demultiplexer_1 (
    .out1(bltz), .out4(beq), .out5(bne), .out6(blez), .out7(bgtz), .in(comparator_6_eq), .sel(Op_Code[2:0]));  // open: out0, out2, out3
  Comparator #(.width(3), .mode("unsigned")) comparator_7 (
    .a(Op_Code[5:3]), .b(3'b001), .eq(Inmediate));  // open: gt, lt
  Demultiplexer #(.select(3), .enable("false")) demultiplexer_2 (
    .out0(addi), .out2(slti), .out3(sltiu), .out4(andi), .out5(ori), .out6(xori), .in(Inmediate),
    .sel(Op_Code[2:0]));  // open: out1, out7
  or or_18 (sltu_or_sltiu, sltu, sltiu);
  Demultiplexer #(.select(2), .enable("false")) demultiplexer_3 (
    .out0(Add), .out2(Sub), .in(Add_or_Sub), .sel(Fun_Code[1:0]));  // open: out1, out3
  Demultiplexer #(.select(2), .enable("false")) demultiplexer_4 (
    .out0(And), .out1(Or), .out3(Nor), .in(cmp_set_1), .sel(Fun_Code[1:0]));  // open: out2
  or or_19 (sltu___sltiu___slt___slti, slt, slti, sltu_or_sltiu);
  or or_20 (blez___bgtz___bltz, bltz, blez, bgtz);
  Demultiplexer #(.select(2), .enable("false")) demultiplexer_5 (
    .out0(Mult), .out1(Mulu), .out2(Div), .out3(Divu), .in(Is_Mul_Or_Div), .sel(Fun_Code[1:0]));
  or or_21 (or___ori, Or, ori);
  or or_22 (xor___xori, Xor, xori);
  or or_23 (add___sub___slt___stlu___and___or___nor___xor, cmp_set_1, cmp_set_2, Add_or_Sub);
  // Probe on {6{1'b1}}
  or or_24 (mul___div, Mult, Div);
  Comparator #(.width(6), .mode("unsigned")) comparator_8 (
    .a(Op_Code), .b(6'b111000), .eq(comparator_8_eq));  // open: gt, lt
  Comparator #(.width(6), .mode("unsigned")) comparator_9 (.a(Op_Code), .b({6{1'b1}}), .eq(Special));  // open: gt, lt
  Comparator #(.width(6), .mode("unsigned")) comparator_10 (.a(Op_Code), .b(6'b000010), .eq(j));  // open: gt, lt
  Comparator #(.width(6), .mode("unsigned")) comparator_11 (
    .a(Fun_Code), .b(6'b010000), .eq(comparator_11_eq));  // open: gt, lt
  and and_5 (SelOpB[1], comparator_8_eq, comparator_12_eq);
  Comparator #(.width(5), .mode("unsigned")) comparator_12 (
    .a({5{1'b0}}), .b(Fun_Code[5:1]), .eq(comparator_12_eq));  // open: gt, lt
  Comparator #(.width(3), .mode("unsigned")) comparator_13 (
    .a(Fun_Code[5:3]), .b(3'b000), .eq(comparator_13_eq));  // open: gt, lt
  Comparator #(.width(5), .mode("unsigned")) comparator_14 (
    .a({Op_Code[5:4], Op_Code[2:0]}), .b(5'b10011), .eq(lw_or_sw));  // open: gt, lt
  or or_25 (mulu___divu, Mulu, Divu);
  or or_26 (and___andi, And, andi);
  Comparator #(.width(4), .mode("unsigned")) comparator_15 (
    .a(Fun_Code[5:2]), .b(4'b1010), .eq(comparator_15_eq));  // open: gt, lt
  and and_6 (mfhi, Op_code_is_0, comparator_11_eq);
  Comparator #(.width(6), .mode("unsigned")) comparator_16 (
    .a(Fun_Code), .b(6'b001000), .eq(comparator_16_eq));  // open: gt, lt
  Demultiplexer #(.enable("false")) demultiplexer_6 (.out0(Is_Pop), .out1(Is_Push), .in(SelOpB[1]), .sel(Fun_Code[0]));
  and and_7 (and_7_out, Special, comparator_13_eq);
  Demultiplexer #(.select(3), .enable("false")) demultiplexer_7 (
    .out1(tty), .out2(rnd), .out4(kbd), .in(and_7_out), .sel(Fun_Code[2:0]));  // open: out0, out3, out5, out6, out7
  Demultiplexer #(.enable("false")) demultiplexer_8 (.out0(lw), .out1(Is_Sw), .in(lw_or_sw), .sel(Op_Code[3]));
  and and_8 (cmp_set_2, Op_code_is_0, comparator_15_eq);
  Demultiplexer #(.select(2), .enable("false")) demultiplexer_9 (
    .out0(Xor), .out2(slt), .out3(sltu), .in(cmp_set_2), .sel(Fun_Code[1:0]));  // open: out1
  and and_9 (jr, Op_code_is_0, comparator_16_eq);
  Comparator #(.width(6), .mode("unsigned")) comparator_17 (
    .a(Fun_Code), .b(6'b010010), .eq(comparator_17_eq));  // open: gt, lt
  and and_10 (mflo, Op_code_is_0, comparator_17_eq);

  // Other names for the same wires on the sheet: Is_Jump = jmp; pop = Is_Pop; push = Is_Push; Pop_or_Push = SelOpB[1];
  //   mfhi___mflow = SelRegIn[1]; sw = Is_Sw

  // Notes on the sheet:
  //   Entradas
  //   For Datapath
  //   Instruction Decoder
endmodule

module CONTROL_UNIT_2 (
  input  CLK,
  input  Finish_Instruction_Fetch,
  input  RESET,
  input  Finish_Mem_Section,
  input  [5:0] Op_Code,
  input  [5:0] Fun_Code,
  output [3:0] Alu_Op,
  output Mem_Write,
  output Is_Jump,
  output Mul_or_Div,
  output Sel_SP_Addr,
  output Sel_Reg_Address,
  output Instr_Cache_Enable,
  output [1:0] SelOpB,
  output Put_Zeros,
  output [1:0] SelRegIn,
  output IsPop,
  output Mem_Cache_Enable,
  output Halt___Stop,
  output Reg_Write,
  output IsPush,
  output Tty_Enable,
  output Mem_Write_LastOp,
  output Load_Pc,
  output is_rnd,
  output [1:0] Sel_Hi,
  output Sel_Ram_Address,
  output Kbd_Enable
);

  wire Begin, demultiplexer_1_out0, demultiplexer_1_out1, demultiplexer_2_out0, demultiplexer_3_out0,
       demultiplexer_4_out0, demultiplexer_5_out0, demultiplexer_6_out0, demultiplexer_7_out0,
       demultiplexer_8_out0, demultiplexer_9_out0, demultiplexer_10_out0, Erase_Mem_Write, FINISH_0,
       FINISH_1, FINISH_2, FINISH_3, Is_Sw, LOGICAL, Logical_Inmediate, LW_or_SW, Mem_En_0, Mem_En_1,
       Mem_En_2, Mem_En_3, Mem_Write_Occurr, Memory_Write_Occurr_0, Memory_Write_Occurr_1, or_11_out,
       POP_OR_PUSH, Reg_Write_0, Reg_Write_1, Reg_Write_3, Reg_Write_4, Reg_Write_5, Reg_Write_7,
       Reg_Write_8, SPECIAL_INST, start_q, Wait_mem_2_q, Wait_mem_4_q, Wait_mem_5_q, Wait_mem_q, Wait_SP_q;
  wire [1:0] Special;
  wire [2:0] CU_Path;

  Demultiplexer #(.enable("false")) demultiplexer_1 (
    .out0(demultiplexer_1_out0), .out1(demultiplexer_1_out1), .in(LW_or_SW), .sel(Is_Sw));
  Demultiplexer #(.enable("false")) demultiplexer_2 (
    .out0(demultiplexer_2_out0), .out1(Put_Zeros), .in(LOGICAL), .sel(Logical_Inmediate));
  or or_1 (Mem_En_0, demultiplexer_3_out0, demultiplexer_1_out0);
  or or_2 (Mem_En_1, demultiplexer_4_out0, demultiplexer_1_out1);
  D_Flip_Flop Wait_mem (.clk(CLK), .D(Mem_En_0), .Q(Wait_mem_q), .reset(RESET));  // open: Qn, preset, en
  Demultiplexer #(.enable("false")) demultiplexer_3 (
    .out0(demultiplexer_3_out0), .out1(Reg_Write_0), .in(Wait_mem_q), .sel(Finish_Mem_Section));
  D_Flip_Flop Wait_mem_2 (.clk(CLK), .D(Mem_En_1), .Q(Wait_mem_2_q), .reset(RESET));  // open: Qn, preset, en
  or or_3 (Instr_Cache_Enable, demultiplexer_5_out0, Load_Pc);
  Demultiplexer #(.enable("false")) demultiplexer_4 (
    .out0(demultiplexer_4_out0), .out1(Memory_Write_Occurr_0), .in(Wait_mem_2_q), .sel(Finish_Mem_Section));
  D_Flip_Flop start (.clk(CLK), .D(Instr_Cache_Enable), .Q(start_q), .preset(RESET));  // open: Qn, en, reset
  Demultiplexer #(.enable("false")) demultiplexer_5 (
    .out0(demultiplexer_5_out0), .out1(Erase_Mem_Write), .in(start_q), .sel(Finish_Instruction_Fetch));
  or or_4 (FINISH_1, demultiplexer_2_out0, Put_Zeros);
  Demultiplexer #(.select(3), .enable("false")) demultiplexer_6 (
    .out0(demultiplexer_6_out0), .out1(LW_or_SW), .out2(Reg_Write_1), .out3(Mul_or_Div), .out4(LOGICAL),
    .out5(POP_OR_PUSH), .out6(Reg_Write_5), .out7(SPECIAL_INST), .in(Erase_Mem_Write), .sel(CU_Path));
  or or_5 (FINISH_0, Reg_Write_0, Memory_Write_Occurr_0);
  or or_6 (Reg_Write, Reg_Write_0, Reg_Write_1, FINISH_1, Reg_Write_3, Reg_Write_4, Reg_Write_5, is_rnd, Reg_Write_7, Reg_Write_8);
  or or_7 (Sel_Ram_Address, Mem_En_0, Mem_En_1, Mem_En_2, Mem_En_3);
  or or_8 (Mem_Write_Occurr, Memory_Write_Occurr_0, Memory_Write_Occurr_1);
  or or_9 (Begin, RESET, ~Finish_Instruction_Fetch);  // OR_Gate
  or or_10 (Mem_Write, Mem_En_1, Mem_En_3);
  or or_11 (or_11_out, demultiplexer_6_out0, FINISH_0, Reg_Write_1, Mul_or_Div, FINISH_1, FINISH_2, Reg_Write_5, FINISH_3);
  Register #(.width(1)) u_Mem_Write (
    .D(Mem_Write_Occurr), .Q(Mem_Write_LastOp), .clk(CLK), .clr(Erase_Mem_Write));  // open: en
  or or_12 (Sel_SP_Addr, Reg_Write_4, Reg_Write_8);
  or or_13 (Sel_Reg_Address, Reg_Write_0, LOGICAL);
  D_Flip_Flop End (.clk(CLK), .D(or_11_out), .Q(Load_Pc), .reset(RESET));  // open: Qn, preset, en
  or or_14 (Mem_Cache_Enable, Mem_En_0, Mem_En_1, Mem_En_2, Mem_En_3);
  Instruction_Decoder instruction_decoder_1 (
    .Op_Code(Op_Code), .Alu_Op(Alu_Op), .SelOpB(SelOpB), .Fun_Code(Fun_Code), .jmp(Is_Jump),
    .SelRegIn(SelRegIn), .Sel_Hi(Sel_Hi), .Path(CU_Path), .Is_Sw(Is_Sw),
    .Logical_Inmediate(Logical_Inmediate), .Is_Push(IsPush), .Especial(Special), .Is_Pop(IsPop));
  Demultiplexer #(.select(2), .enable("false")) demultiplexer_7 (
    .out0(demultiplexer_7_out0), .out1(Tty_Enable), .out2(is_rnd), .out3(Reg_Write_7), .in(SPECIAL_INST),
    .sel(Special));
  Demultiplexer #(.enable("false")) demultiplexer_8 (
    .out0(demultiplexer_8_out0), .out1(Reg_Write_8), .in(POP_OR_PUSH), .sel(IsPush));
  or or_15 (Mem_En_2, demultiplexer_9_out0, demultiplexer_8_out0);
  D_Flip_Flop Wait_mem_3 (
    .clk(CLK), .D(demultiplexer_7_out0), .Q(Halt___Stop), .en(demultiplexer_7_out0), .reset(RESET));  // open: Qn, preset
  D_Flip_Flop Wait_SP (.clk(CLK), .D(Reg_Write_8), .Q(Wait_SP_q), .reset(RESET));  // open: Qn, preset, en
  D_Flip_Flop Wait_for_Kdb (.clk(CLK), .D(Reg_Write_7), .Q(Kbd_Enable), .reset(RESET));  // open: Qn, preset, en
  D_Flip_Flop Wait_mem_4 (.clk(CLK), .D(Mem_En_2), .Q(Wait_mem_4_q), .reset(RESET));  // open: Qn, preset, en
  Demultiplexer #(.enable("false")) demultiplexer_9 (
    .out0(demultiplexer_9_out0), .out1(Reg_Write_3), .in(Wait_mem_4_q), .sel(Finish_Mem_Section));
  or or_16 (FINISH_3, Tty_Enable, is_rnd, Kbd_Enable);
  or or_17 (Mem_En_3, demultiplexer_10_out0, Wait_SP_q);
  D_Flip_Flop Wait_Reg_Write (.clk(CLK), .D(Reg_Write_3), .Q(Reg_Write_4), .reset(RESET));  // open: Qn, preset, en
  D_Flip_Flop Wait_mem_5 (.clk(CLK), .D(Mem_En_3), .Q(Wait_mem_5_q), .reset(RESET));  // open: Qn, preset, en
  Demultiplexer #(.enable("false")) demultiplexer_10 (
    .out0(demultiplexer_10_out0), .out1(Memory_Write_Occurr_1), .in(Wait_mem_5_q), .sel(Finish_Mem_Section));
  or or_18 (FINISH_2, Reg_Write_4, Memory_Write_Occurr_1);

  // Other names for the same wires on the sheet: finish_inst_fetch = Finish_Instruction_Fetch; halt = Halt___Stop;
  //   Ins_Cache_En = Instr_Cache_Enable; Is_Push = IsPush; Mem_Cache_En = Mem_Cache_Enable; PutZeros = Put_Zeros;
  //   Reg_Write_2 = FINISH_1; Reg_Write_6 = is_rnd; rnd = is_rnd; Sel_Reg_Address_0 = Reg_Write_0;
  //   Sel_Reg_Address_1 = LOGICAL; Sel_Sp_Addr_0 = Reg_Write_4; Sel_Sp_Addr_1 = Reg_Write_8;
  //   SelAddr = Sel_Ram_Address; SelAddr_0 = Mem_En_0; Mem_Write_0 = Mem_En_1; SelAddr_1 = Mem_En_1;
  //   SelAddr_2 = Mem_En_2; Mem_Write_1 = Mem_En_3; SelAddr_3 = Mem_En_3

  // Notes on the sheet:
  //   Input Data
  //   LOGICAL
  //   Addi, sltiu, slti
  //   andi, ori, xori
  //   Lw or Sw
  //   no finish
  //   finish
  //   CONTROL_UNIT
  //   Input from Data Path
  //   finish
  //   finish
  //   Control Signals for Datapath
  //   mfhi or mflo
  //   add, sub, slt, sltu, and, or, nor, xor
  //   mul, mulu, div, divu
  //   0 para instructions
  //   1 para datos
  //   nop and jumps
  //   finish
  //   finish
  //   finish
  //   CONTROL_SIGNALS
  //   Special Instructions
  //   pop
  //   push
  //   POP OR PUSH
  //   tty finish
  //   rnd finish
  //   finish
  //   finish
endmodule

module Data_Path (
  input  CLK,
  input  Reset,
  input  MEM_WRITE_LAST_OP,
  input  [31:0] Ram_Out_0,
  input  [31:0] Ram_Out_1,
  input  [31:0] Ram_Out_2,
  input  [31:0] Ram_Out_3,
  input  [3:0] Read_Time,
  input  [3:0] Write_Time,
  input  Read_Write_Reg,
  input  MulorDiv,
  input  [3:0] Alu_Op,
  input  Is_Push,
  input  kbd_available,
  input  [6:0] kbd_data,
  input  Memory_RW,
  input  Is_Pop,
  input  Is_Jump_Instr,
  input  random,
  input  Load_New_PC,
  input  Put_Zeros,
  input  [1:0] Sel_Op_B,
  input  Sel_Ram_Address,
  input  Sel_SP_Addr,
  input  [1:0] Sel_Hi,
  input  [1:0] Sel_Reg_Input,
  input  Sel_Reg_Address,
  input  Ins_Cache_En,
  input  Mem_Cache_En,
  output [31:0] Ram_IN_0,
  output [31:0] Ram_IN_1,
  output [31:0] Ram_IN_2,
  output [31:0] Ram_IN_3,
  output CS,
  output [3:0] Mask_for_RAM,
  output [15:0] Ram__ADDRESS,
  output RW_Out,
  output [6:0] Tty,
  output Finish_Instruction_Fetch,
  output Finish_Mem_Section,
  output [5:0] Op_Code,
  output [5:0] Fun_Code
);

  wire CSofD, CSofI, N, Push_or_Pop, Z;
  wire [1:0] Sel_Reg_In;
  wire [4:0] multiplexer_5_out, Reg_Address;
  wire [15:0] Last_Ram_Write_Addr, Ram_Address_0, Ram_Address_1;
  wire [25:6] Address;
  wire [31:0] Alu_Res, B, Hi, HiOut, kbd_data_t, Lo, Mem_Address, Mem_Input, Mem_Out, multiplexer_4_out,
       multiplexer_8_out, New_PC, Op_A, Op_B, PC, random_out, Reg_Input, SignExt, SP;
  wire [31:7] A;

  Program_Counter program_counter_1 (.ENABLE(Load_New_PC), .PC_OUTPUT(PC), .RESET(Reset), .INPUT(New_PC), .CLK(CLK));
  Multiplexer #(.width(32), .enable("false")) multiplexer_1 (.in0({A, Tty}), .in1(SP), .out(Op_A), .sel(Push_or_Pop));
  Multiplexer #(.select(2), .width(32), .enable("false")) multiplexer_2 (
    .in0(B), .in1(SignExt), .in2(32'h4), .out(Op_B), .sel(Sel_Op_B));  // open: in3
  Multiplexer #(.width(32)) multiplexer_3 (.in0(Alu_Res), .in1(SP), .out(Mem_Address), .sel(Push_or_Pop));  // open: en
  SIGN_EXTENDER sign_extender_1 (._16_Bits({Address[15:6], Fun_Code}), .Put_zeros(Put_Zeros), .out_3(SignExt));
  // Probe on Op_B
  // Probe on Mem_Address
  Multiplexer #(.select(2), .width(32), .enable("false")) multiplexer_4 (
    .in0(Alu_Res), .in1(Mem_Out), .in2(Hi), .in3(Lo), .out(multiplexer_4_out), .sel(Sel_Reg_In));
  Multiplexer #(.width(5), .enable("false")) multiplexer_5 (
    .in0(Address[15:11]), .in1(Address[20:16]), .out(multiplexer_5_out), .sel(Sel_Reg_Address));
  Multiplexer #(.width(32), .enable("false")) multiplexer_6 (.in0(B), .in1({A, Tty}), .out(Mem_Input), .sel(Is_Push));
  Random #(.width(32)) u_random (.clk(CLK), .out(random_out));  // open: next, clr
  Multiplexer #(.width(5), .enable("false")) multiplexer_7 (
    .in0(multiplexer_5_out), .in1({5{1'b1}}), .out(Reg_Address), .sel(Sel_SP_Addr));
  Multiplexer #(.width(32), .enable("false")) multiplexer_8 (
    .in0(multiplexer_4_out), .in1(random_out), .out(multiplexer_8_out), .sel(random));
  Branch_Control branch_control_1 (
    .DEST({Address, Fun_Code}), .RS({A, Tty}), .PC(PC), .JMP(Is_Jump_Instr), .Z(Z), .N(N),
    .Jmp_Bits(Op_Code[2:0]), .NEW_PC(New_PC), .OFFSET(SignExt));
  Register_File register_file_1 (
    .DA(Reg_Address), .DI(Reg_Input), .Clk(CLK), .Reset(Reset), .R_W(Read_Write_Reg), .SA(Address[25:21]),
    .SB(Address[20:16]), .B(B), .Hi_Input(HiOut), .Lo_Input(Alu_Res), .A({A, Tty}), .Hi_Output(Hi),
    .Lo_Output(Lo), .MULT_OR_DIV(MulorDiv), .STACK_POINTER(SP));
  Multiplexer #(.width(32), .enable("false")) multiplexer_9 (
    .in0(multiplexer_8_out), .in1(kbd_data_t), .out(Reg_Input), .sel(kbd_available));
  or or_1 (Push_or_Pop, Is_Push, Is_Pop);
  CACHE_INSTRUCTION cache_instruction_1 (
    .CLK(CLK), .Direccion_de_ultima_escritura_en_RAM(Last_Ram_Write_Addr), .RW(MEM_WRITE_LAST_OP),
    .RT(Read_Time), .RST(Reset), .Data_Address(PC), .RAM_OUT_0(Ram_Out_0), .RAM_OUT_1(Ram_Out_1),
    .RAM_OUT_2(Ram_Out_2), .RAM_OUT_3(Ram_Out_3), .Cache_enable(Ins_Cache_En), .CS(CSofI),
    .Data_Out({Op_Code, Address, Fun_Code}), .Finish(Finish_Instruction_Fetch), .Ram_Address(Ram_Address_0));
  Multiplexer #(.width(2), .enable("false")) multiplexer_10 (
    .in0(Sel_Reg_Input), .in1(2'b00), .out(Sel_Reg_In), .sel(Sel_SP_Addr));
  // Probe on B
  // Probe on Fun_Code
  // Probe on Op_Code
  ALU alu_1 (
    .HIGH(HiOut), .Operator_A(Op_A), .Output(Alu_Res), .Operator_B(Op_B), .Zero(Z), .Neg(N),
    .Selector(Alu_Op), .Sel_Hi(Sel_Hi));
  // Probe on Mem_Address
  // Probe on Alu_Res
  // Probe on HiOut
  Register #(.width(16)) register_1 (.D(Ram_Address_1), .en(RW_Out), .Q(Last_Ram_Write_Addr), .clk(CLK));  // open: clr
  CACHE_DATA cache_data_1 (
    .clk(CLK), .RT(Read_Time), .R_W(Memory_RW), .WT(Write_Time), .RST(Reset), .Write_Data(Mem_Input),
    .Data_Address(Mem_Address), .RAM_OUT_0(Ram_Out_0), .RAM_OUT_1(Ram_Out_1), .RAM_OUT_2(Ram_Out_2),
    .RAM_OUT_3(Ram_Out_3), .Is_Cache_Enable(Mem_Cache_En), .Data_Out(Mem_Out), .Finish(Finish_Mem_Section),
    .RAM_Input_0(Ram_IN_0), .RAM_Input_1(Ram_IN_1), .RAM_Input_2(Ram_IN_2), .RAM_Input_3(Ram_IN_3),
    .Mask(Mask_for_RAM), .RW_out(RW_Out), .RAM_Address(Ram_Address_1), .CS(CSofD));
  Multiplexer #(.width(16), .enable("false")) multiplexer_11 (
    .in0(Ram_Address_0), .in1(Ram_Address_1), .out(Ram__ADDRESS), .sel(Sel_Ram_Address));
  // Probe on {A, Tty}
  Multiplexer #(.width(32), .enable("false")) multiplexer_12 (
    .in0({{25{1'b0}}, kbd_data}), .in1({32{1'b1}}), .out(kbd_data_t), .sel(kbd_available));
  or or_2 (CS, CSofI, CSofD);

  // Other names for the same wires on the sheet: A[6:0] = Tty; Address[5:0] = Fun_Code; X[4:0] = Address[10:6];
  //   Rd[4:0] = Address[15:11]; Rt_t[4:0] = Address[20:16]; Rs[4:0] = Address[25:21];
  //   Finish_Data = Finish_Mem_Section; Finish_Ins = Finish_Instruction_Fetch; jmp = Is_Jump_Instr;
  //   Load_PC = Load_New_PC; Mask[3:0] = Mask_for_RAM; Mem_Write = Memory_RW; Ram_Address[15:0] = Ram__ADDRESS;
  //   RAM_Input_0[31:0] = Ram_IN_0; RAM_Input_1[31:0] = Ram_IN_1; RAM_Input_2[31:0] = Ram_IN_2;
  //   RAM_Input_3[31:0] = Ram_IN_3; Reg_Write = Read_Write_Reg; rnd = random; RT[3:0] = Read_Time;
  //   Sel_Address = Sel_Ram_Address; Sel_Reg_In_0[1:0] = Sel_Reg_Input; WT[3:0] = Write_Time

  // Notes on the sheet:
  //   INPUTS_S-MIPS
  //   INPUTS_CU
  //   DATAPATH
  //   CONDICIONALES
  //   OUPUTS_S-MIPS
  //   Salidas
  //   OUTPUT_CU
endmodule

module ALU (
  input  [31:0] Operator_A,
  input  [31:0] Operator_B,
  input  [3:0] Selector,
  input  [1:0] Sel_Hi,
  output [31:0] HIGH,
  output [31:0] Output,
  output Zero,
  output Neg
);

  wire comparator_1_lt, comparator_2_lt;
  wire [31:0] ADD, AND, divider_1_rem, HI_DIV, HI_DIVU, HI_MUL, HI_MULU, LO_DIV, LO_DIVU, LO_MUL, LO_MULU,
       NOR, OR, SLT, SLTU, SUB, XOR;

  assign AND = Operator_A & Operator_B;  // AND_Gate and_1, 32 bits wide
  assign OR = Operator_A | Operator_B;  // OR_Gate or_1, 32 bits wide
  assign NOR = ~(Operator_A | Operator_B);  // NOR_Gate nor_1, 32 bits wide
  assign XOR = Operator_A ^ Operator_B;  // XOR_Gate xor_1, 32 bits wide
  Comparator #(.width(32)) comparator_1 (.a(Operator_A), .b(Operator_B), .lt(comparator_1_lt));  // open: gt, eq
  Comparator #(.width(32), .mode("unsigned")) comparator_2 (
    .a(Operator_A), .b(Operator_B), .lt(comparator_2_lt));  // open: gt, eq
  // Probe on comparator_2_lt
  // Probe on Operator_A
  // Probe on Operator_B
  // Probe on comparator_1_lt
  assign SLTU = {{31{1'b0}}, comparator_2_lt};  // Bit_Extender bit_extender_1
  assign SLT = {{31{1'b0}}, comparator_1_lt};  // Bit_Extender bit_extender_2
  // Probe on SLT
  Adder #(.width(32)) adder_1 (.a(Operator_A), .b(Operator_B), .out(ADD));  // open: cin, cout
  Subtractor #(.width(32)) subtractor_1 (.a(Operator_A), .b(Operator_B), .out(SUB));  // open: bin, bout
  // Probe on SLTU
  Divider #(.width(32)) divider_1 (.a(Operator_A), .b(Operator_B), .rem(divider_1_rem));  // open: out, upper
  // Probe on divider_1_rem
  // Probe on LO_DIVU
  Multiplexer #(.select(4), .width(32), .enable("false")) multiplexer_1 (
    .in0(ADD), .in1(SUB), .in2(LO_MUL), .in3(LO_DIV), .in4(LO_MULU), .in5(LO_DIVU), .in6(AND), .in7(OR),
    .in8(NOR), .in9(XOR), .in10(SLT), .in11(SLTU), .in12(Operator_A), .out(Output), .sel(Selector));  // open: in13, in14, in15
  // Probe on HI_DIVU
  // Probe on Output
  Divider #(.width(32)) divider_2 (.a(Operator_A), .b(Operator_B), .out(LO_DIVU), .rem(HI_DIVU));  // open: upper
  Division division_1 (.A(Operator_A), .B(Operator_B), .Hi(HI_DIV), .Lo(LO_DIV));
  Multiplication multiplication_1 (.A(Operator_A), .Hi(HI_MUL), .B(Operator_B), .Lo(LO_MUL));
  Multiplier #(.width(32)) multiplier_1 (.a(Operator_A), .b(Operator_B), .out(LO_MULU), .cout(HI_MULU));  // open: cin
  Comparator #(.width(32)) comparator_3 (.a(Output), .b({32{1'b0}}), .eq(Zero), .lt(Neg));  // open: gt
  Multiplexer #(.select(2), .width(32), .enable("false")) multiplexer_2 (
    .in0(HI_MUL), .in1(HI_MULU), .in2(HI_DIV), .in3(HI_DIVU), .out(HIGH), .sel(Sel_Hi));

  // Other names for the same wires on the sheet: A[31:0] = Operator_A; B[31:0] = Operator_B; Selec[3:0] = Selector

  // Notes on the sheet:
  //   Inputs
  //   ALU
  //   FLAGS
endmodule

module Multiplication (
  input  [31:0] A,
  input  [31:0] B,
  output [31:0] Hi,
  output [31:0] Lo
);

  wire [31:0] multiplexer_1_out, multiplexer_2_out, negator_1_out, negator_2_out;

  // Probe on A
  // Probe on B
  Negator #(.width(32)) negator_1 (.in(B), .out(negator_1_out));
  Negator #(.width(32)) negator_2 (.in(A), .out(negator_2_out));
  // Probe on negator_2_out
  // Probe on negator_1_out
  Multiplexer #(.width(32), .enable("false")) multiplexer_1 (
    .in0(A), .in1(negator_2_out), .out(multiplexer_1_out), .sel(A[31]));
  // Probe on multiplexer_2_out
  Multiplexer #(.width(32), .enable("false")) multiplexer_2 (
    .in0(B), .in1(negator_1_out), .out(multiplexer_2_out), .sel(B[31]));
  // Probe on multiplexer_1_out
  Multiplier #(.width(32)) multiplier_1 (
    .a(multiplexer_1_out), .b(multiplexer_2_out), .out(Lo), .cout(Hi));  // open: cin

  // Other names for the same wires on the sheet: Sign_A = A[31]; Sign_B = B[31]

  // Notes on the sheet:
  //   Unsigned_Multiplication
endmodule

module Division (
  input  [31:0] A,
  input  [31:0] B,
  output [31:0] Hi,
  output [31:0] Lo
);

  wire [31:0] multiplexer_1_out, multiplexer_2_out, negator_1_out, negator_2_out;

  // Probe on B
  // Probe on A
  Negator #(.width(32)) negator_1 (.in(A), .out(negator_1_out));
  Negator #(.width(32)) negator_2 (.in(B), .out(negator_2_out));
  Multiplexer #(.width(32)) multiplexer_1 (
    .in0(A), .in1(negator_1_out), .out(multiplexer_1_out), .sel(A[31]));  // open: en
  Multiplexer #(.width(32)) multiplexer_2 (
    .in0(B), .in1(negator_2_out), .out(multiplexer_2_out), .sel(B[31]));  // open: en
  // Probe on multiplexer_1_out
  // Probe on multiplexer_2_out
  Divider #(.width(32)) divider_1 (.a(multiplexer_1_out), .b(multiplexer_2_out), .out(Lo), .rem(Hi));  // open: upper
  // Probe on Hi
  // Probe on Lo

  // Other names for the same wires on the sheet: Sign_A = A[31]; Sign_B = B[31]

  // Notes on the sheet:
  //   Signed_Division
endmodule

module Register_File (
  input  [4:0] DA,
  input  [31:0] DI,
  input  Clk,
  input  Reset,
  input  R_W,
  input  [4:0] SA,
  input  [4:0] SB,
  input  MULT_OR_DIV,
  input  [31:0] Hi_Input,
  input  [31:0] Lo_Input,
  output [31:0] A,
  output [31:0] B,
  output [31:0] STACK_POINTER,
  output [31:0] Hi_Output,
  output [31:0] Lo_Output
);

  wire E01, E02, E03, E04, E05, E06, E07, E08, E09, E10, E11, E12, E13, E14, E15, E16, E17, E18, E19, E20,
       E21, E22, E23, E24, E25, E26, E27, E28, E29, E30, E31;
  wire [31:0] D00, D01, D02, D03, D04, D05, D06, D07, D08, D09, D10, D11, D12, D13, D14, D15, D16, D17, D18,
       D19, D20, D21, D22, D23, D24, D25, D26, D27, D28, D29, D30;

  Register #(.width(32)) register_1 (.D(DI), .en(1'b0), .Q(D00), .clk(Clk), .clr(Reset));
  Register #(.width(32)) register_2 (.D(DI), .en(E01), .Q(D01), .clk(Clk), .clr(Reset));
  Register #(.width(32)) register_3 (.D(DI), .en(E02), .Q(D02), .clk(Clk), .clr(Reset));
  Register #(.width(32)) register_4 (.D(DI), .en(E03), .Q(D03), .clk(Clk), .clr(Reset));
  Register #(.width(32)) register_5 (.D(DI), .en(E04), .Q(D04), .clk(Clk), .clr(Reset));
  Register #(.width(32)) register_6 (.D(DI), .en(E05), .Q(D05), .clk(Clk), .clr(Reset));
  Register #(.width(32)) register_7 (.D(DI), .en(E06), .Q(D06), .clk(Clk), .clr(Reset));
  Register #(.width(32)) register_8 (.D(DI), .en(E07), .Q(D07), .clk(Clk), .clr(Reset));
  Register #(.width(32)) register_9 (.D(DI), .en(E08), .Q(D08), .clk(Clk), .clr(Reset));
  Register #(.width(32)) register_10 (.D(DI), .en(E09), .Q(D09), .clk(Clk), .clr(Reset));
  Register #(.width(32)) register_11 (.D(DI), .en(E10), .Q(D10), .clk(Clk), .clr(Reset));
  Register #(.width(32)) register_12 (.D(DI), .en(E11), .Q(D11), .clk(Clk), .clr(Reset));
  Register #(.width(32)) register_13 (.D(DI), .en(E12), .Q(D12), .clk(Clk), .clr(Reset));
  Register #(.width(32)) register_14 (.D(DI), .en(E13), .Q(D13), .clk(Clk), .clr(Reset));
  Register #(.width(32)) register_15 (.D(DI), .en(E14), .Q(D14), .clk(Clk), .clr(Reset));
  Register #(.width(32)) register_16 (.D(DI), .en(E15), .Q(D15), .clk(Clk), .clr(Reset));
  Multiplexer #(.select(5), .width(32), .enable("false")) multiplexer_1 (
    .in0(D00), .in1(D01), .in2(D02), .in3(D03), .in4(D04), .in5(D05), .in6(D06), .in7(D07), .in8(D08),
    .in9(D09), .in10(D10), .in11(D11), .in12(D12), .in13(D13), .in14(D14), .in15(D15), .in16(D16),
    .in17(D17), .in18(D18), .in19(D19), .in20(D20), .in21(D21), .in22(D22), .in23(D23), .in24(D24),
    .in25(D25), .in26(D26), .in27(D27), .in28(D28), .in29(D29), .in30(D30), .in31(STACK_POINTER), .out(A),
    .sel(SA));
  Register #(.width(32)) Hi (.D(Hi_Input), .en(MULT_OR_DIV), .Q(Hi_Output), .clk(Clk));  // open: clr
  Register #(.width(32)) Lo (.D(Lo_Input), .en(MULT_OR_DIV), .Q(Lo_Output), .clk(Clk));  // open: clr
  Register #(.width(32)) register_17 (.D(DI), .en(E16), .Q(D16), .clk(Clk), .clr(Reset));
  Register #(.width(32)) register_18 (.D(DI), .en(E17), .Q(D17), .clk(Clk), .clr(Reset));
  Register #(.width(32)) register_19 (.D(DI), .en(E18), .Q(D18), .clk(Clk), .clr(Reset));
  Register #(.width(32)) register_20 (.D(DI), .en(E19), .Q(D19), .clk(Clk), .clr(Reset));
  Register #(.width(32)) register_21 (.D(DI), .en(E20), .Q(D20), .clk(Clk), .clr(Reset));
  Register #(.width(32)) register_22 (.D(DI), .en(E21), .Q(D21), .clk(Clk), .clr(Reset));
  Register #(.width(32)) register_23 (.D(DI), .en(E22), .Q(D22), .clk(Clk), .clr(Reset));
  Register #(.width(32)) register_24 (.D(DI), .en(E23), .Q(D23), .clk(Clk), .clr(Reset));
  Register #(.width(32)) register_25 (.D(DI), .en(E24), .Q(D24), .clk(Clk), .clr(Reset));
  Register #(.width(32)) register_26 (.D(DI), .en(E25), .Q(D25), .clk(Clk), .clr(Reset));
  Register #(.width(32)) register_27 (.D(DI), .en(E26), .Q(D26), .clk(Clk), .clr(Reset));
  Register #(.width(32)) register_28 (.D(DI), .en(E27), .Q(D27), .clk(Clk), .clr(Reset));
  Register #(.width(32)) register_29 (.D(DI), .en(E28), .Q(D28), .clk(Clk), .clr(Reset));
  Register #(.width(32)) register_30 (.D(DI), .en(E29), .Q(D29), .clk(Clk), .clr(Reset));
  Register #(.width(32)) register_31 (.D(DI), .en(E30), .Q(D30), .clk(Clk), .clr(Reset));
  Register #(.width(32)) register_32 (.D(DI), .en(E31), .Q(STACK_POINTER), .clk(Clk), .clr(Reset));
  Multiplexer #(.select(5), .width(32), .enable("false")) multiplexer_2 (
    .in0(D00), .in1(D01), .in2(D02), .in3(D03), .in4(D04), .in5(D05), .in6(D06), .in7(D07), .in8(D08),
    .in9(D09), .in10(D10), .in11(D11), .in12(D12), .in13(D13), .in14(D14), .in15(D15), .in16(D16),
    .in17(D17), .in18(D18), .in19(D19), .in20(D20), .in21(D21), .in22(D22), .in23(D23), .in24(D24),
    .in25(D25), .in26(D26), .in27(D27), .in28(D28), .in29(D29), .in30(D30), .in31(STACK_POINTER), .out(B),
    .sel(SB));
  Demultiplexer #(.select(5), .enable("false")) demultiplexer_1 (
    .out1(E01), .out2(E02), .out3(E03), .out4(E04), .out5(E05), .out6(E06), .out7(E07), .out8(E08),
    .out9(E09), .out10(E10), .out11(E11), .out12(E12), .out13(E13), .out14(E14), .out15(E15), .out16(E16),
    .out17(E17), .out18(E18), .out19(E19), .out20(E20), .out21(E21), .out22(E22), .out23(E23), .out24(E24),
    .out25(E25), .out26(E26), .out27(E27), .out28(E28), .out29(E29), .out30(E30), .out31(E31), .in(R_W),
    .sel(DA));  // open: out0

  // Other names for the same wires on the sheet: C = Clk; D31[31:0] = STACK_POINTER; IN[31:0] = DI;
  //   MULT = MULT_OR_DIV; R = Reset; WRITE = R_W

  // Notes on the sheet:
  //   Inputs
  //   Register File
  //   Outputs
endmodule

module Branch_Control (
  input  JMP,
  input  [31:0] PC,
  input  [25:0] DEST,
  input  [31:0] OFFSET,
  input  [31:0] RS,
  input  Z,
  input  [2:0] Jmp_Bits,
  input  N,
  output [31:0] NEW_PC
);

  wire and_1_out, and_2_out, and_3_out, and_4_out, and_5_out, and_6_out;
  wire [1:0] Jmp_sel;
  wire [31:0] PC_4, PC_4_4_OFFSET, shifter_1_out;

  // Probe on OFFSET
  Adder #(.width(32)) adder_1 (.a(PC), .b(32'h4), .out(PC_4));  // open: cin, cout
  Shifter #(.width(32)) shifter_1 (.in(OFFSET), .\dist (5'b00010), .out(shifter_1_out));
  // Probe on shifter_1_out
  Adder #(.width(32)) adder_2 (.a(PC_4), .b(shifter_1_out), .out(PC_4_4_OFFSET));  // open: cin, cout
  Multiplexer #(.select(2), .width(32)) multiplexer_1 (
    .in0(PC_4), .in1(PC_4_4_OFFSET), .in2(RS), .in3({PC[31:28], DEST, 2'b00}), .out(NEW_PC), .sel(Jmp_sel));  // open: en
  and and_1 (and_1_out, JMP, ~Jmp_Bits[2], ~Jmp_Bits[0], ~Jmp_Bits[1]);  // AND_Gate
  and and_2 (and_2_out, JMP, ~Jmp_Bits[2], ~Jmp_Bits[0], Jmp_Bits[1]);  // AND_Gate
  and and_3 (and_3_out, ~N, ~Z, JMP, Jmp_Bits[2], Jmp_Bits[0]);  // AND_Gate
  and and_4 (and_4_out, ~N, Z, JMP, ~Jmp_Bits[0]);  // AND_Gate
  and and_5 (and_5_out, N, ~Z, JMP, ~Jmp_Bits[1], Jmp_Bits[0]);  // AND_Gate
  and and_6 (and_6_out, N, ~Z, JMP, Jmp_Bits[1], ~Jmp_Bits[0]);  // AND_Gate
  or or_1 (Jmp_sel[1], and_1_out, and_2_out);
  or or_2 (Jmp_sel[0], and_2_out, and_3_out, and_4_out, and_5_out, and_6_out);
  // Probe on Jmp_sel

  // Other names for the same wires on the sheet: B0 = Jmp_Bits[0]; B1 = Jmp_Bits[1]; B2 = Jmp_Bits[2];
  //   Jump[31:2] = {PC[31:28], DEST}; Next_PC[31:0] = NEW_PC

  // Notes on the sheet:
  //   INPUTS
  //   OUTPUT
  //   Branch Control
  //   BGTZ OR BNE 
  //   BLTZ OR BNE
  //   JR
  //   J
  //   BEQ
  //   BLEZ
endmodule

module Program_Counter (
  input  [31:0] INPUT,
  input  RESET,
  input  ENABLE,
  input  CLK,
  output [31:0] PC_OUTPUT
);

  Register #(.width(32)) register_1 (.D(INPUT), .en(ENABLE), .Q(PC_OUTPUT), .clk(CLK), .clr(RESET));

  // Notes on the sheet:
  //   Program Counter
endmodule

module SIGN_EXTENDER (
  input  [15:0] _16_Bits,
  input  Put_zeros,
  output [31:0] out_3
);

  wire [15:0] Sign_Ext;

  assign Sign_Ext = {{15{_16_Bits[15]}}, _16_Bits[15]};  // Bit_Extender bit_extender_1
  // Probe on Sign_Ext
  Multiplexer #(.width(16), .enable("false")) multiplexer_1 (
    .in0(Sign_Ext), .in1({16{1'b0}}), .out(out_3[31:16]), .sel(Put_zeros));

  assign out_3[15:0] = _16_Bits;

  // Other names for the same wires on the sheet: Res[15:0] = out_3[31:16]
endmodule

module CACHE_INSTRUCTION (
  input  CLK,
  input  [15:0] Direccion_de_ultima_escritura_en_RAM,
  input  RW,
  input  [3:0] RT,
  input  RST,
  input  [31:0] Data_Address,
  input  [31:0] RAM_OUT_0,
  input  [31:0] RAM_OUT_1,
  input  [31:0] RAM_OUT_2,
  input  [31:0] RAM_OUT_3,
  input  Cache_enable,
  output CS,
  output [31:0] Data_Out,
  output Finish,
  output [15:0] Ram_Address
);

  wire and_1_out, comparator_1_eq, comparator_2_eq, comparator_3_eq, CS_t, d_ff_1_q, Enable, INVALID, line0,
       line1, line2, line3, line4, line5, line6, line7, or_1_out, Valid, Valid0, Valid1, Valid2, Valid3,
       Valid4, Valid5, Valid6, Valid7, ValidOut, ValidOut_Ram;
  wire [2:0] multiplexer_1_out;
  wire [3:0] adder_1_out, counter_1_q;
  wire [12:0] STag0, STag1, STag2, STag3, STag4, STag5, STag6, STag7, TagOut, TagOut_Ram;
  wire [31:0] Data0, Data1, Data2, Data3, Data4, Data5, Data6, Data7, Data8, Data9, Data10, Data11, Data12,
       Data13, Data14, Data15, Data16, Data17, Data18, Data19, Data20, Data21, Data22, Data23, Data24,
       Data25, Data26, Data27, Data28, Data29, Data30, Data31, multiplexer_6_out, multiplexer_7_out,
       multiplexer_8_out, multiplexer_9_out;

  // Probe on Data_Address[3:2]
  // Probe on Data_Address[6:4]
  or or_1 (or_1_out, Enable, ~Valid);  // OR_Gate
  // Probe on Data_Address[19:7]
  Demultiplexer #(.select(3), .enable("false")) demultiplexer_1 (
    .out0(line0), .out1(line1), .out2(line2), .out3(line3), .out4(line4), .out5(line5), .out6(line6),
    .out7(line7), .in(and_1_out), .sel(multiplexer_1_out));
  and and_1 (and_1_out, or_1_out, Cache_enable);
  Multiplexer #(.width(3), .enable("false")) multiplexer_1 (
    .in0(Data_Address[6:4]), .in1(Direccion_de_ultima_escritura_en_RAM[2:0]), .out(multiplexer_1_out),
    .sel(RW));
  and and_2 (CS, ~RST, Cache_enable, CS_t);  // AND_Gate
  // Probe on STag5
  Register #(.width(13)) register_1 (.D(Data_Address[19:7]), .en(line0), .Q(STag0), .clk(CLK), .clr(RST));
  Register #(.width(13)) register_2 (.D(Data_Address[19:7]), .en(line1), .Q(STag1), .clk(CLK), .clr(RST));
  Register #(.width(13)) register_3 (.D(Data_Address[19:7]), .en(line2), .Q(STag2), .clk(CLK), .clr(RST));
  Register #(.width(13)) register_4 (.D(Data_Address[19:7]), .en(line3), .Q(STag3), .clk(CLK), .clr(RST));
  Register #(.width(13)) register_5 (.D(Data_Address[19:7]), .en(line4), .Q(STag4), .clk(CLK), .clr(RST));
  Register #(.width(13)) register_6 (.D(Data_Address[19:7]), .en(line5), .Q(STag5), .clk(CLK), .clr(RST));
  Register #(.width(13)) register_7 (.D(Data_Address[19:7]), .en(line6), .Q(STag6), .clk(CLK), .clr(RST));
  Register #(.width(13)) register_8 (.D(Data_Address[19:7]), .en(line7), .Q(STag7), .clk(CLK), .clr(RST));
  Comparator #(.width(13), .mode("unsigned")) comparator_1 (
    .a(TagOut), .b(Data_Address[19:7]), .eq(comparator_1_eq));  // open: gt, lt
  Register #(.width(32)) register_9 (.D(RAM_OUT_0), .en(line0), .Q(Data0), .clk(CLK), .clr(RST));
  Register #(.width(32)) register_10 (.D(RAM_OUT_0), .en(line1), .Q(Data4), .clk(CLK), .clr(RST));
  Register #(.width(32)) register_11 (.D(RAM_OUT_0), .en(line2), .Q(Data8), .clk(CLK), .clr(RST));
  Register #(.width(32)) register_12 (.D(RAM_OUT_0), .en(line3), .Q(Data12), .clk(CLK), .clr(RST));
  Register #(.width(32)) register_13 (.D(RAM_OUT_0), .en(line4), .Q(Data16), .clk(CLK), .clr(RST));
  Register #(.width(32)) register_14 (.D(RAM_OUT_0), .en(line5), .Q(Data20), .clk(CLK), .clr(RST));
  Register #(.width(32)) register_15 (.D(RAM_OUT_0), .en(line6), .Q(Data24), .clk(CLK), .clr(RST));
  Register #(.width(32)) register_16 (.D(RAM_OUT_0), .en(line7), .Q(Data28), .clk(CLK), .clr(RST));
  and and_3 (Finish, ValidOut, comparator_1_eq);
  Register #(.width(32)) register_17 (.D(RAM_OUT_1), .en(line0), .Q(Data1), .clk(CLK), .clr(RST));
  Register #(.width(32)) register_18 (.D(RAM_OUT_1), .en(line1), .Q(Data5), .clk(CLK), .clr(RST));
  Register #(.width(32)) register_19 (.D(RAM_OUT_1), .en(line2), .Q(Data9), .clk(CLK), .clr(RST));
  Register #(.width(32)) register_20 (.D(RAM_OUT_1), .en(line3), .Q(Data13), .clk(CLK), .clr(RST));
  Register #(.width(32)) register_21 (.D(RAM_OUT_1), .en(line4), .Q(Data17), .clk(CLK), .clr(RST));
  Register #(.width(32)) register_22 (.D(RAM_OUT_1), .en(line5), .Q(Data21), .clk(CLK), .clr(RST));
  Register #(.width(32)) register_23 (.D(RAM_OUT_1), .en(line6), .Q(Data25), .clk(CLK), .clr(RST));
  Register #(.width(32)) register_24 (.D(RAM_OUT_1), .en(line7), .Q(Data29), .clk(CLK), .clr(RST));
  Register #(.width(32)) register_25 (.D(RAM_OUT_2), .en(line0), .Q(Data2), .clk(CLK), .clr(RST));
  Register #(.width(32)) register_26 (.D(RAM_OUT_2), .en(line1), .Q(Data6), .clk(CLK), .clr(RST));
  Register #(.width(32)) register_27 (.D(RAM_OUT_2), .en(line2), .Q(Data10), .clk(CLK), .clr(RST));
  Register #(.width(32)) register_28 (.D(RAM_OUT_2), .en(line3), .Q(Data14), .clk(CLK), .clr(RST));
  Register #(.width(32)) register_29 (.D(RAM_OUT_2), .en(line4), .Q(Data18), .clk(CLK), .clr(RST));
  Register #(.width(32)) register_30 (.D(RAM_OUT_2), .en(line5), .Q(Data22), .clk(CLK), .clr(RST));
  Register #(.width(32)) register_31 (.D(RAM_OUT_2), .en(line6), .Q(Data26), .clk(CLK), .clr(RST));
  Register #(.width(32)) register_32 (.D(RAM_OUT_2), .en(line7), .Q(Data30), .clk(CLK), .clr(RST));
  not not_1 (CS_t, Finish);
  Register #(.width(32)) register_33 (.D(RAM_OUT_3), .en(line0), .Q(Data3), .clk(CLK), .clr(RST));
  Register #(.width(32)) register_34 (.D(RAM_OUT_3), .en(line1), .Q(Data7), .clk(CLK), .clr(RST));
  Register #(.width(32)) register_35 (.D(RAM_OUT_3), .en(line2), .Q(Data11), .clk(CLK), .clr(RST));
  Register #(.width(32)) register_36 (.D(RAM_OUT_3), .en(line3), .Q(Data15), .clk(CLK), .clr(RST));
  Register #(.width(32)) register_37 (.D(RAM_OUT_3), .en(line4), .Q(Data19), .clk(CLK), .clr(RST));
  Register #(.width(32)) register_38 (.D(RAM_OUT_3), .en(line5), .Q(Data23), .clk(CLK), .clr(RST));
  Register #(.width(32)) register_39 (.D(RAM_OUT_3), .en(line6), .Q(Data27), .clk(CLK), .clr(RST));
  Register #(.width(32)) register_40 (.D(RAM_OUT_3), .en(line7), .Q(Data31), .clk(CLK), .clr(RST));
  Adder #(.width(4)) adder_1 (.a(RT), .b(4'b0001), .out(adder_1_out));  // open: cin, cout
  Counter #(.width(4), .max('hf)) counter_1 (
    .load(CS_t), .D(adder_1_out), .count(d_ff_1_q), .Q(counter_1_q), .clk(CLK));  // open: carry, clr
  D_Flip_Flop d_ff_1 (.clk(CLK), .D(CS_t), .Q(d_ff_1_q));  // open: Qn, preset, en, reset
  Register #(.width(1)) register_41 (.D(Valid), .en(line0), .Q(Valid0), .clk(CLK), .clr(RST));
  Register #(.width(1)) register_42 (.D(Valid), .en(line1), .Q(Valid1), .clk(CLK), .clr(RST));
  Register #(.width(1)) register_43 (.D(Valid), .en(line2), .Q(Valid2), .clk(CLK), .clr(RST));
  Register #(.width(1)) register_44 (.D(Valid), .en(line3), .Q(Valid3), .clk(CLK), .clr(RST));
  Register #(.width(1)) register_45 (.D(Valid), .en(line4), .Q(Valid4), .clk(CLK), .clr(RST));
  Register #(.width(1)) register_46 (.D(Valid), .en(line5), .Q(Valid5), .clk(CLK), .clr(RST));
  Register #(.width(1)) register_47 (.D(Valid), .en(line6), .Q(Valid6), .clk(CLK), .clr(RST));
  Register #(.width(1)) register_48 (.D(Valid), .en(line7), .Q(Valid7), .clk(CLK), .clr(RST));
  // Probe on counter_1_q
  Comparator #(.width(4), .mode("unsigned")) comparator_2 (
    .a(counter_1_q), .b(4'b0000), .eq(comparator_2_eq));  // open: gt, lt
  and and_4 (Enable, comparator_2_eq, d_ff_1_q);
  Multiplexer #(.select(3)) multiplexer_2 (
    .in0(Valid0), .in1(Valid1), .in2(Valid2), .in3(Valid3), .in4(Valid4), .in5(Valid5), .in6(Valid6),
    .in7(Valid7), .out(ValidOut), .sel(Data_Address[6:4]));  // open: en
  Multiplexer #(.select(3), .width(13)) multiplexer_3 (
    .in0(STag0), .in1(STag1), .in2(STag2), .in3(STag3), .in4(STag4), .in5(STag5), .in6(STag6), .in7(STag7),
    .out(TagOut), .sel(Data_Address[6:4]));  // open: en
  Comparator #(.width(13), .mode("unsigned")) comparator_3 (
    .a(TagOut_Ram), .b(Direccion_de_ultima_escritura_en_RAM[15:3]), .eq(comparator_3_eq));  // open: gt, lt
  nand nand_1 (Valid, RW, INVALID);
  and and_5 (INVALID, ValidOut_Ram, comparator_3_eq);
  Multiplexer #(.select(3)) multiplexer_4 (
    .in0(Valid0), .in1(Valid1), .in2(Valid2), .in3(Valid3), .in4(Valid4), .in5(Valid5), .in6(Valid6),
    .in7(Valid7), .out(ValidOut_Ram), .sel(Direccion_de_ultima_escritura_en_RAM[2:0]));  // open: en
  Multiplexer #(.select(3), .width(13)) multiplexer_5 (
    .in0(STag0), .in1(STag1), .in2(STag2), .in3(STag3), .in4(STag4), .in5(STag5), .in6(STag6), .in7(STag7),
    .out(TagOut_Ram), .sel(Direccion_de_ultima_escritura_en_RAM[2:0]));  // open: en
  Multiplexer #(.select(3), .width(32)) multiplexer_6 (
    .in0(Data0), .in1(Data4), .in2(Data8), .in3(Data12), .in4(Data16), .in5(Data20), .in6(Data24),
    .in7(Data28), .out(multiplexer_6_out), .sel(Data_Address[6:4]));  // open: en
  Multiplexer #(.select(3), .width(32)) multiplexer_7 (
    .in0(Data1), .in1(Data5), .in2(Data9), .in3(Data13), .in4(Data17), .in5(Data21), .in6(Data25),
    .in7(Data29), .out(multiplexer_7_out), .sel(Data_Address[6:4]));  // open: en
  Multiplexer #(.select(3), .width(32)) multiplexer_8 (
    .in0(Data2), .in1(Data6), .in2(Data10), .in3(Data14), .in4(Data18), .in5(Data22), .in6(Data26),
    .in7(Data30), .out(multiplexer_8_out), .sel(Data_Address[6:4]));  // open: en
  Multiplexer #(.select(3), .width(32)) multiplexer_9 (
    .in0(Data3), .in1(Data7), .in2(Data11), .in3(Data15), .in4(Data19), .in5(Data23), .in6(Data27),
    .in7(Data31), .out(multiplexer_9_out), .sel(Data_Address[6:4]));  // open: en
  Multiplexer #(.select(2), .width(32)) multiplexer_10 (
    .in0(multiplexer_6_out), .in1(multiplexer_7_out), .in2(multiplexer_8_out), .in3(multiplexer_9_out),
    .out({Data_Out[7:0], Data_Out[15:8], Data_Out[23:16], Data_Out[31:24]}), .sel(Data_Address[3:2]));  // open: en
  // Probe on Data_Out

  assign Ram_Address = Data_Address[19:4];

  // Other names for the same wires on the sheet: data0_t[31:0] = RAM_OUT_0; data1_t[31:0] = RAM_OUT_1;
  //   data2_t[31:0] = RAM_OUT_2; data3_t[31:0] = RAM_OUT_3; Offset[1:0] = Data_Address[3:2];
  //   Line[2:0] = Data_Address[6:4]; Tag[12:0] = Data_Address[19:7];
  //   Line_Ram[2:0] = Direccion_de_ultima_escritura_en_RAM[2:0];
  //   Tag_Ram[12:0] = Direccion_de_ultima_escritura_en_RAM[15:3]; Hit = Finish; reset = RST

  // Notes on the sheet:
  //   INPUTS
  //   OUTPUTS
  //   TAGS
  //   Si se encontro el elemento en cache
  //   CACHE INSTRUCTION
  //   VALUES
  //   Si se produce un Miss
  //   Esto es para copiar de la RAM a la cache
  //   VALID
  //   Pon invalida la linea de cache
  //   Ocurre cuando la ultima operacion de escritura en Ram
  //   Se efectuo en una direccion que esta en la cache
endmodule

module CACHE_DATA (
  input  clk,
  input  [3:0] RT,
  input  R_W,
  input  [3:0] WT,
  input  RST,
  input  [31:0] Write_Data,
  input  [31:0] Data_Address,
  input  [31:0] RAM_OUT_0,
  input  [31:0] RAM_OUT_1,
  input  [31:0] RAM_OUT_2,
  input  [31:0] RAM_OUT_3,
  input  Is_Cache_Enable,
  output [31:0] Data_Out,
  output Finish,
  output [31:0] RAM_Input_0,
  output [31:0] RAM_Input_1,
  output [31:0] RAM_Input_2,
  output [31:0] RAM_Input_3,
  output [3:0] Mask,
  output RW_out,
  output [15:0] RAM_Address,
  output CS
);

  wire and_2_out, and_3_out, and_4_out, and_5_out, and_6_out, and_7_out, and_8_out, and_9_out,
       comparator_1_eq, comparator_2_eq, comparator_3_eq, CS_t, CSR, d_ff_4_q, d_ff_5_q, Finish_Reading,
       line0, line1, line2, line3, line4, line5, line6, line7, or_2_out, or_3_out, or_4_out, or_5_out, valid,
       Valid0, Valid1, Valid2, Valid3, Valid4, Valid5, Valid6, Valid7, ValidOut, Write_End;
  wire [3:0] counter_1_q, counter_2_q;
  wire [12:0] STag0, STag1, STag2, STag3, STag4, STag5, STag6, STag7, TagOut;
  wire [31:0] Data0, Data1, Data2, Data3, Data4, Data5, Data6, Data7, Data8, Data9, Data10, Data11, Data12,
       Data13, Data14, Data15, Data16, Data17, Data18, Data19, Data20, Data21, Data22, Data23, Data24,
       Data25, Data26, Data27, Data28, Data29, Data30, Data31, multiplexer_3_out, multiplexer_4_out,
       multiplexer_5_out, multiplexer_6_out;

  // Probe on Data_Address
  // Probe on Data_Out
  // Probe on Data_Address[3:2]
  // Probe on Data_Address[6:4]
  // Probe on Data_Address[19:7]
  and and_1 (CS, ~RST, Is_Cache_Enable, CS_t);  // AND_Gate
  // Probe on Data_Address[19:4]
  Register #(.width(13)) register_1 (.D(Data_Address[19:7]), .en(line0), .Q(STag0), .clk(clk), .clr(RST));
  Register #(.width(13)) register_2 (.D(Data_Address[19:7]), .en(line1), .Q(STag1), .clk(clk), .clr(RST));
  // Probe on STag2
  Register #(.width(13)) register_3 (.D(Data_Address[19:7]), .en(line2), .Q(STag2), .clk(clk), .clr(RST));
  Register #(.width(13)) register_4 (.D(Data_Address[19:7]), .en(line3), .Q(STag3), .clk(clk), .clr(RST));
  Register #(.width(13)) register_5 (.D(Data_Address[19:7]), .en(line4), .Q(STag4), .clk(clk), .clr(RST));
  Register #(.width(13)) register_6 (.D(Data_Address[19:7]), .en(line5), .Q(STag5), .clk(clk), .clr(RST));
  Register #(.width(13)) register_7 (.D(Data_Address[19:7]), .en(line6), .Q(STag6), .clk(clk), .clr(RST));
  Register #(.width(13)) register_8 (.D(Data_Address[19:7]), .en(line7), .Q(STag7), .clk(clk), .clr(RST));
  Demultiplexer #(.select(2)) demultiplexer_1 (
    .out0(Mask[0]), .out1(Mask[1]), .out2(Mask[2]), .out3(Mask[3]), .in(R_W), .sel(Data_Address[3:2]));  // open: en
  or or_1 (CS_t, RW_out, CSR);
  Demultiplexer #(.select(2), .width(32), .enable("false")) demultiplexer_2 (
    .out0(RAM_Input_0), .out1(RAM_Input_1), .out2(RAM_Input_2), .out3(RAM_Input_3),
    .in({Write_Data[7:0], Write_Data[15:8], Write_Data[23:16], Write_Data[31:24]}), .sel(Data_Address[3:2]));
  Register #(.width(32)) register_9 (.D(RAM_OUT_0), .en(line0), .Q(Data0), .clk(clk), .clr(RST));
  Register #(.width(32)) register_10 (.D(RAM_OUT_0), .en(line1), .Q(Data4), .clk(clk), .clr(RST));
  Register #(.width(32)) register_11 (.D(RAM_OUT_0), .en(line2), .Q(Data8), .clk(clk), .clr(RST));
  Register #(.width(32)) register_12 (.D(RAM_OUT_0), .en(line3), .Q(Data12), .clk(clk), .clr(RST));
  Register #(.width(32)) register_13 (.D(RAM_OUT_0), .en(line4), .Q(Data16), .clk(clk), .clr(RST));
  Register #(.width(32)) register_14 (.D(RAM_OUT_0), .en(line5), .Q(Data20), .clk(clk), .clr(RST));
  Register #(.width(32)) register_15 (.D(RAM_OUT_0), .en(line6), .Q(Data24), .clk(clk), .clr(RST));
  Register #(.width(32)) register_16 (.D(RAM_OUT_0), .en(line7), .Q(Data28), .clk(clk), .clr(RST));
  Register #(.width(32)) register_17 (.D(RAM_OUT_1), .en(line0), .Q(Data1), .clk(clk), .clr(RST));
  Register #(.width(32)) register_18 (.D(RAM_OUT_1), .en(line1), .Q(Data5), .clk(clk), .clr(RST));
  Register #(.width(32)) register_19 (.D(RAM_OUT_1), .en(line2), .Q(Data9), .clk(clk), .clr(RST));
  Register #(.width(32)) register_20 (.D(RAM_OUT_1), .en(line3), .Q(Data13), .clk(clk), .clr(RST));
  Register #(.width(32)) register_21 (.D(RAM_OUT_1), .en(line4), .Q(Data17), .clk(clk), .clr(RST));
  Register #(.width(32)) register_22 (.D(RAM_OUT_1), .en(line5), .Q(Data21), .clk(clk), .clr(RST));
  Register #(.width(32)) register_23 (.D(RAM_OUT_1), .en(line6), .Q(Data25), .clk(clk), .clr(RST));
  Register #(.width(32)) register_24 (.D(RAM_OUT_1), .en(line7), .Q(Data29), .clk(clk), .clr(RST));
  Register #(.width(32)) register_25 (.D(RAM_OUT_2), .en(line0), .Q(Data2), .clk(clk), .clr(RST));
  Register #(.width(32)) register_26 (.D(RAM_OUT_2), .en(line1), .Q(Data6), .clk(clk), .clr(RST));
  Register #(.width(32)) register_27 (.D(RAM_OUT_2), .en(line2), .Q(Data10), .clk(clk), .clr(RST));
  Register #(.width(32)) register_28 (.D(RAM_OUT_2), .en(line3), .Q(Data14), .clk(clk), .clr(RST));
  Register #(.width(32)) register_29 (.D(RAM_OUT_2), .en(line4), .Q(Data18), .clk(clk), .clr(RST));
  Register #(.width(32)) register_30 (.D(RAM_OUT_2), .en(line5), .Q(Data22), .clk(clk), .clr(RST));
  Register #(.width(32)) register_31 (.D(RAM_OUT_2), .en(line6), .Q(Data26), .clk(clk), .clr(RST));
  Register #(.width(32)) register_32 (.D(RAM_OUT_2), .en(line7), .Q(Data30), .clk(clk), .clr(RST));
  // Probe on Data31
  Register #(.width(32)) register_33 (.D(RAM_OUT_3), .en(line0), .Q(Data3), .clk(clk), .clr(RST));
  Register #(.width(32)) register_34 (.D(RAM_OUT_3), .en(line1), .Q(Data7), .clk(clk), .clr(RST));
  Register #(.width(32)) register_35 (.D(RAM_OUT_3), .en(line2), .Q(Data11), .clk(clk), .clr(RST));
  Register #(.width(32)) register_36 (.D(RAM_OUT_3), .en(line3), .Q(Data15), .clk(clk), .clr(RST));
  Register #(.width(32)) register_37 (.D(RAM_OUT_3), .en(line4), .Q(Data19), .clk(clk), .clr(RST));
  Register #(.width(32)) register_38 (.D(RAM_OUT_3), .en(line5), .Q(Data23), .clk(clk), .clr(RST));
  Register #(.width(32)) register_39 (.D(RAM_OUT_3), .en(line6), .Q(Data27), .clk(clk), .clr(RST));
  Register #(.width(32)) register_40 (.D(RAM_OUT_3), .en(line7), .Q(Data31), .clk(clk), .clr(RST));
  and and_2 (and_2_out, ~RW_out, Is_Cache_Enable, ~R_W);  // AND_Gate
  and and_3 (and_3_out, RW_out, Is_Cache_Enable, Write_End);
  and and_4 (and_4_out, CSR, Is_Cache_Enable);
  and and_5 (and_5_out, ~CSR, ~RW_out, Is_Cache_Enable, R_W);  // AND_Gate
  and and_6 (and_6_out, RW_out, Is_Cache_Enable, ~Write_End);  // AND_Gate
  or or_2 (or_2_out, and_2_out, and_3_out, and_4_out);
  or or_3 (or_3_out, and_5_out, and_6_out);
  Register #(.width(1)) register_41 (.D(valid), .en(line0), .Q(Valid0), .clk(clk), .clr(RST));
  Register #(.width(1)) register_42 (.D(valid), .en(line1), .Q(Valid1), .clk(clk), .clr(RST));
  Register #(.width(1)) register_43 (.D(valid), .en(line2), .Q(Valid2), .clk(clk), .clr(RST));
  Register #(.width(1)) register_44 (.D(valid), .en(line3), .Q(Valid3), .clk(clk), .clr(RST));
  Register #(.width(1)) register_45 (.D(valid), .en(line4), .Q(Valid4), .clk(clk), .clr(RST));
  Register #(.width(1)) register_46 (.D(valid), .en(line5), .Q(Valid5), .clk(clk), .clr(RST));
  Register #(.width(1)) register_47 (.D(valid), .en(line6), .Q(Valid6), .clk(clk), .clr(RST));
  Register #(.width(1)) register_48 (.D(valid), .en(line7), .Q(Valid7), .clk(clk), .clr(RST));
  D_Flip_Flop d_ff_1 (.clk(clk), .D(or_2_out), .Q(CSR));  // open: Qn, preset, en, reset
  D_Flip_Flop d_ff_2 (.clk(clk), .D(or_3_out), .Q(RW_out));  // open: Qn, preset, en, reset
  not not_1 (valid, RW_out);
  or or_4 (or_4_out, Finish_Reading, RW_out);
  Multiplexer #(.select(3)) multiplexer_1 (
    .in0(Valid0), .in1(Valid1), .in2(Valid2), .in3(Valid3), .in4(Valid4), .in5(Valid5), .in6(Valid6),
    .in7(Valid7), .out(ValidOut), .sel(Data_Address[6:4]));  // open: en
  Multiplexer #(.select(3), .width(13)) multiplexer_2 (
    .in0(STag0), .in1(STag1), .in2(STag2), .in3(STag3), .in4(STag4), .in5(STag5), .in6(STag6), .in7(STag7),
    .out(TagOut), .sel(Data_Address[6:4]));  // open: en
  Comparator #(.width(13), .mode("unsigned")) comparator_1 (
    .a(TagOut), .b(Data_Address[19:7]), .eq(comparator_1_eq));  // open: gt, lt
  and and_7 (and_7_out, or_4_out, Is_Cache_Enable);
  and and_8 (and_8_out, ValidOut, comparator_1_eq);
  or or_5 (or_5_out, ~R_W, CSR);  // OR_Gate
  Demultiplexer #(.select(3), .enable("false")) demultiplexer_3 (
    .out0(line0), .out1(line1), .out2(line2), .out3(line3), .out4(line4), .out5(line5), .out6(line6),
    .out7(line7), .in(and_7_out), .sel(Data_Address[6:4]));
  and and_9 (and_9_out, and_8_out, or_5_out);
  D_Flip_Flop d_ff_3 (.clk(clk), .D(and_9_out), .Q(Finish));  // open: Qn, preset, en, reset
  Counter #(.width(4), .max('hf)) counter_1 (
    .load(RW_out), .D(WT), .count(d_ff_4_q), .Q(counter_1_q), .clk(clk));  // open: carry, clr
  D_Flip_Flop d_ff_4 (.clk(clk), .D(RW_out), .Q(d_ff_4_q));  // open: Qn, preset, en, reset
  // Probe on counter_1_q
  Comparator #(.width(4), .mode("unsigned")) comparator_2 (
    .a(counter_1_q), .b(4'b0000), .eq(comparator_2_eq));  // open: gt, lt
  and and_10 (Write_End, comparator_2_eq, d_ff_4_q);
  Multiplexer #(.select(3), .width(32)) multiplexer_3 (
    .in0(Data0), .in1(Data4), .in2(Data8), .in3(Data12), .in4(Data16), .in5(Data20), .in6(Data24),
    .in7(Data28), .out(multiplexer_3_out), .sel(Data_Address[6:4]));  // open: en
  Multiplexer #(.select(3), .width(32)) multiplexer_4 (
    .in0(Data1), .in1(Data5), .in2(Data9), .in3(Data13), .in4(Data17), .in5(Data21), .in6(Data25),
    .in7(Data29), .out(multiplexer_4_out), .sel(Data_Address[6:4]));  // open: en
  Multiplexer #(.select(3), .width(32)) multiplexer_5 (
    .in0(Data2), .in1(Data6), .in2(Data10), .in3(Data14), .in4(Data18), .in5(Data22), .in6(Data26),
    .in7(Data30), .out(multiplexer_5_out), .sel(Data_Address[6:4]));  // open: en
  Multiplexer #(.select(3), .width(32)) multiplexer_6 (
    .in0(Data3), .in1(Data7), .in2(Data11), .in3(Data15), .in4(Data19), .in5(Data23), .in6(Data27),
    .in7(Data31), .out(multiplexer_6_out), .sel(Data_Address[6:4]));  // open: en
  // Probe on counter_2_q
  Counter #(.width(4), .max('hf)) counter_2 (
    .load(CSR), .D(RT), .count(d_ff_5_q), .Q(counter_2_q), .clk(clk));  // open: carry, clr
  D_Flip_Flop d_ff_5 (.clk(clk), .D(CSR), .Q(d_ff_5_q));  // open: Qn, preset, en, reset
  Multiplexer #(.select(2), .width(32)) multiplexer_7 (
    .in0(multiplexer_3_out), .in1(multiplexer_4_out), .in2(multiplexer_5_out), .in3(multiplexer_6_out),
    .out({Data_Out[7:0], Data_Out[15:8], Data_Out[23:16], Data_Out[31:24]}), .sel(Data_Address[3:2]));  // open: en
  Comparator #(.width(4), .mode("unsigned")) comparator_3 (
    .a(counter_2_q), .b(4'b0000), .eq(comparator_3_eq));  // open: gt, lt
  and and_11 (Finish_Reading, comparator_3_eq, d_ff_5_q);

  assign RAM_Address = Data_Address[19:4];

  // Other names for the same wires on the sheet: WD[31:0] = Write_Data; Cache_Enable = Is_Cache_Enable;
  //   data0_t[31:0] = RAM_OUT_0; data1_t[31:0] = RAM_OUT_1; data2_t[31:0] = RAM_OUT_2; data3_t[31:0] = RAM_OUT_3;
  //   Offset[1:0] = Data_Address[3:2]; Line[2:0] = Data_Address[6:4]; Tag[12:0] = Data_Address[19:7]; Hit = Finish;
  //   Read = CSR; reset = RST; RW = R_W; CSW = RW_out; Write = RW_out

  // Notes on the sheet:
  //   INPUTS
  //   OUPUTS
  //   TAGS
  //   CACHE DATA
  //   Necesita acceder a RAM
  //   WRITE TO RAM
  //   VALUES
  //   ASM RW
  //   VALID
  //   selector linea de cache una vez
  //   que se haya terminado de escribir en RAM
  //   si la linea de cache tiene dato
  //   tener el tag de la linea
  //   Si se encontro el elemento en cache
  //   Si se produce un Miss
  //   Esto es para habilitar la copia de la RAM a la cache
endmodule
